// Logisim project FPGAGHO_Mayoria.circ as structural Verilog
module FPGA (
  input  Entrada_A,
  input  Entrada_B,
  input  Entrada_C,
  input  Entrada_D,
  output W,
  output X,
  output Y,
  output Z
);

  wire BusA, BusB, BusC, BusD, BusE, BusF, BusG, BusH, BusInA, BusInB, BusInC, BusInD, clock_1_out,
       clock_2_out, clock_3_out, clock_4_out;

  Clock MasterClock ();  // open: out
  assign BusInA = 1'b1 ? Entrada_A : 1'bz;  // Controlled_Buffer controlled_buffer_1
  assign BusInA = 1'b0 ? Entrada_B : 1'bz;  // Controlled_Buffer controlled_buffer_2
  assign BusInA = 1'b0 ? Entrada_C : 1'bz;  // Controlled_Buffer controlled_buffer_3
  assign BusInA = 1'b0 ? Entrada_D : 1'bz;  // Controlled_Buffer controlled_buffer_4
  assign BusInB = 1'b0 ? Entrada_A : 1'bz;  // Controlled_Buffer controlled_buffer_5
  assign BusInC = 1'b0 ? Entrada_A : 1'bz;  // Controlled_Buffer controlled_buffer_6
  assign BusInB = 1'b1 ? Entrada_B : 1'bz;  // Controlled_Buffer controlled_buffer_7
  assign BusInC = 1'b0 ? Entrada_B : 1'bz;  // Controlled_Buffer controlled_buffer_8
  assign BusInB = 1'b0 ? Entrada_C : 1'bz;  // Controlled_Buffer controlled_buffer_9
  assign BusInC = 1'b1 ? Entrada_C : 1'bz;  // Controlled_Buffer controlled_buffer_10
  assign BusInB = 1'b0 ? Entrada_D : 1'bz;  // Controlled_Buffer controlled_buffer_11
  assign BusInC = 1'b0 ? Entrada_D : 1'bz;  // Controlled_Buffer controlled_buffer_12
  LED led_1 (.in(W));
  LED led_2 (.in(X));
  LED led_3 (.in(Y));
  LED led_4 (.in(Z));
  assign BusInD = 1'b0 ? Entrada_A : 1'bz;  // Controlled_Buffer controlled_buffer_13
  assign BusInD = 1'b0 ? Entrada_B : 1'bz;  // Controlled_Buffer controlled_buffer_14
  assign BusInD = 1'b0 ? Entrada_C : 1'bz;  // Controlled_Buffer controlled_buffer_15
  assign BusInD = 1'b0 ? Entrada_D : 1'bz;  // Controlled_Buffer controlled_buffer_16
  Clock clock_1 (.out(clock_1_out));
  Clock clock_2 (.out(clock_2_out));
  CLB CLB_A (
    .OutBusSel(4'b1100), .Clk(clock_1_out), .OutSel(2'b01), .LUTF(16'he8),
    .BusInterno({Z, Y, X, W, BusH, BusG, BusF, BusE, BusD, BusC, BusB, BusA, BusInD, BusInC, BusInB, BusInA}),
    .FFRSel(4'b0000), .LUTS(16'h4012),
    .RetBusInterno({Z, Y, X, W, BusH, BusG, BusF, BusE, BusD, BusC, BusB, BusA, BusInD, BusInC, BusInB, BusInA}));
  CLB CLB_C (
    .OutBusSel(4'b0101), .Clk(clock_2_out), .OutSel(2'b10), .LUTF(16'h2),
    .BusInterno({Z, Y, X, W, BusH, BusG, BusF, BusE, BusD, BusC, BusB, BusA, BusInD, BusInC, BusInB, BusInA}),
    .FFRSel(4'b0000), .LUTS(16'h444d),
    .RetBusInterno({Z, Y, X, W, BusH, BusG, BusF, BusE, BusD, BusC, BusB, BusA, BusInD, BusInC, BusInB, BusInA}));
  assign BusA = 1'b1 ? 1'b0 : 1'bz;  // Controlled_Buffer controlled_buffer_17
  assign BusB = 1'b0 ? 1'b0 : 1'bz;  // Controlled_Buffer controlled_buffer_18
  assign BusC = 1'b0 ? 1'b0 : 1'bz;  // Controlled_Buffer controlled_buffer_19
  assign BusD = 1'b0 ? 1'b0 : 1'bz;  // Controlled_Buffer controlled_buffer_20
  assign BusE = 1'b0 ? 1'b0 : 1'bz;  // Controlled_Buffer controlled_buffer_21
  assign BusF = 1'b0 ? 1'b0 : 1'bz;  // Controlled_Buffer controlled_buffer_22
  assign BusG = 1'b0 ? 1'b0 : 1'bz;  // Controlled_Buffer controlled_buffer_23
  assign BusH = 1'b0 ? 1'b0 : 1'bz;  // Controlled_Buffer controlled_buffer_24
  Clock clock_3 (.out(clock_3_out));
  Clock clock_4 (.out(clock_4_out));
  CLB CLB_B (
    .OutBusSel(4'b0110), .Clk(clock_3_out), .OutSel(2'b10), .LUTF(16'h2),
    .BusInterno({Z, Y, X, W, BusH, BusG, BusF, BusE, BusD, BusC, BusB, BusA, BusInD, BusInC, BusInB, BusInA}),
    .FFRSel(4'b0000), .LUTS(16'h444c),
    .RetBusInterno({Z, Y, X, W, BusH, BusG, BusF, BusE, BusD, BusC, BusB, BusA, BusInD, BusInC, BusInB, BusInA}));
  CLB CLB_D (
    .OutBusSel(4'b0111), .Clk(clock_4_out), .OutSel(2'b10), .LUTF(16'h2),
    .BusInterno({Z, Y, X, W, BusH, BusG, BusF, BusE, BusD, BusC, BusB, BusA, BusInD, BusInC, BusInB, BusInA}),
    .FFRSel(4'b0000), .LUTS(16'h444e),
    .RetBusInterno({Z, Y, X, W, BusH, BusG, BusF, BusE, BusD, BusC, BusB, BusA, BusInD, BusInC, BusInB, BusInA}));

  // Other names for the same wires on the sheet: BusInt[15:0] = {Z, Y, X, W, BusH, BusG, BusF, BusE, BusD, BusC, BusB, BusA, BusInD, BusInC, BusInB, BusInA};
  //   BusOutW = W; BusOutX = X; BusOutY = Y; BusOutZ = Z

  // Notes on the sheet:
  //   SelEntradas
endmodule

module CLB (
  input  [3:0] OutBusSel,
  input  Clk,
  input  [1:0] OutSel,
  input  [15:0] LUTF,
  input  [15:0] BusInterno,
  input  [3:0] FFRSel,
  input  [15:0] LUTS,
  output [15:0] RetBusInterno
);

  wire d_ff_1_q, d_ff_1_qn, multiplexer_1_out, multiplexer_6_out, multiplexer_7_out;
  wire [3:0] multiplexer_5_out;

  Multiplexer #(.select(4)) multiplexer_1 (
    .in0(LUTF[0]), .in1(LUTF[1]), .in2(LUTF[2]), .in3(LUTF[3]), .in4(LUTF[4]), .in5(LUTF[5]), .in6(LUTF[6]),
    .in7(LUTF[7]), .in8(LUTF[8]), .in9(LUTF[9]), .in10(LUTF[10]), .in11(LUTF[11]), .in12(LUTF[12]),
    .in13(LUTF[13]), .in14(LUTF[14]), .in15(LUTF[15]), .out(multiplexer_1_out), .sel(multiplexer_5_out));
  Multiplexer #(.select(4)) multiplexer_2 (
    .in0(BusInterno[0]), .in1(BusInterno[1]), .in2(BusInterno[2]), .in3(BusInterno[3]), .in4(BusInterno[4]),
    .in5(BusInterno[5]), .in6(BusInterno[6]), .in7(BusInterno[7]), .in8(BusInterno[8]), .in9(BusInterno[9]),
    .in10(BusInterno[10]), .in11(BusInterno[11]), .in12(BusInterno[12]), .in13(BusInterno[13]),
    .in14(BusInterno[14]), .in15(BusInterno[15]), .out(multiplexer_5_out[3]), .sel(LUTS[15:12]));
  D_Flip_Flop d_ff_1 (
    .D(multiplexer_1_out), .clk(Clk), .Q(d_ff_1_q), .Qn(d_ff_1_qn), .reset(multiplexer_7_out));  // open: preset
  Multiplexer #(.select(4)) multiplexer_3 (
    .in0(BusInterno[0]), .in1(BusInterno[1]), .in2(BusInterno[2]), .in3(BusInterno[3]), .in4(BusInterno[4]),
    .in5(BusInterno[5]), .in6(BusInterno[6]), .in7(BusInterno[7]), .in8(BusInterno[8]), .in9(BusInterno[9]),
    .in10(BusInterno[10]), .in11(BusInterno[11]), .in12(BusInterno[12]), .in13(BusInterno[13]),
    .in14(BusInterno[14]), .in15(BusInterno[15]), .out(multiplexer_5_out[2]), .sel(LUTS[11:8]));
  Multiplexer #(.select(4)) multiplexer_4 (
    .in0(BusInterno[0]), .in1(BusInterno[1]), .in2(BusInterno[2]), .in3(BusInterno[3]), .in4(BusInterno[4]),
    .in5(BusInterno[5]), .in6(BusInterno[6]), .in7(BusInterno[7]), .in8(BusInterno[8]), .in9(BusInterno[9]),
    .in10(BusInterno[10]), .in11(BusInterno[11]), .in12(BusInterno[12]), .in13(BusInterno[13]),
    .in14(BusInterno[14]), .in15(BusInterno[15]), .out(multiplexer_5_out[1]), .sel(LUTS[7:4]));
  Multiplexer #(.select(4)) multiplexer_5 (
    .in0(BusInterno[0]), .in1(BusInterno[1]), .in2(BusInterno[2]), .in3(BusInterno[3]), .in4(BusInterno[4]),
    .in5(BusInterno[5]), .in6(BusInterno[6]), .in7(BusInterno[7]), .in8(BusInterno[8]), .in9(BusInterno[9]),
    .in10(BusInterno[10]), .in11(BusInterno[11]), .in12(BusInterno[12]), .in13(BusInterno[13]),
    .in14(BusInterno[14]), .in15(BusInterno[15]), .out(multiplexer_5_out[0]), .sel(LUTS[3:0]));
  Multiplexer #(.select(2)) multiplexer_6 (
    .in1(multiplexer_1_out), .in2(d_ff_1_q), .in3(d_ff_1_qn), .out(multiplexer_6_out), .sel(OutSel));  // open: in0
  Demultiplexer #(.select(4), .tristate("true")) demultiplexer_1 (
    .out0(RetBusInterno[0]), .out1(RetBusInterno[1]), .out2(RetBusInterno[2]), .out3(RetBusInterno[3]),
    .out4(RetBusInterno[4]), .out5(RetBusInterno[5]), .out6(RetBusInterno[6]), .out7(RetBusInterno[7]),
    .out8(RetBusInterno[8]), .out9(RetBusInterno[9]), .out10(RetBusInterno[10]), .out11(RetBusInterno[11]),
    .out12(RetBusInterno[12]), .out13(RetBusInterno[13]), .out14(RetBusInterno[14]),
    .out15(RetBusInterno[15]), .in(multiplexer_6_out), .sel(OutBusSel));
  Multiplexer #(.select(4)) multiplexer_7 (
    .in0(BusInterno[0]), .in1(BusInterno[1]), .in2(BusInterno[2]), .in3(BusInterno[3]), .in4(BusInterno[4]),
    .in5(BusInterno[5]), .in6(BusInterno[6]), .in7(BusInterno[7]), .in8(BusInterno[8]), .in9(BusInterno[9]),
    .in10(BusInterno[10]), .in11(BusInterno[11]), .in12(BusInterno[12]), .in13(BusInterno[13]),
    .in14(BusInterno[14]), .in15(BusInterno[15]), .out(multiplexer_7_out), .sel(FFRSel));
endmodule
